// Logisim project DecodeModule.circ as structural Verilog: 2 circuits, main circuit R_decoder
module R_decoder (
  input  [31:0] instruction,
  output [31:0] outp
);

  wire clock_1_out, controllogic_1_registerload;
  wire [3:0] controllogic_1_aluselect;
  wire [4:0] r_splitter_1_rd_i, r_splitter_1_rs1_i, r_splitter_1_rs2_i;
  wire [31:0] registerfile32_1_rs1, registerfile32_1_rs2;

  R_Splitter r_splitter_1 (
    .instruction(instruction), .rd_i(r_splitter_1_rd_i), .rs1_i(r_splitter_1_rs1_i),
    .rs2_i(r_splitter_1_rs2_i));  // open: opcode, funct_3, funct_7
  Clock clock_1 (.out(clock_1_out));
  ControlLogic controllogic_1 (
    .instruction(instruction), .ALUselect(controllogic_1_aluselect),
    .registerLoad(controllogic_1_registerload));
  RegisterFile32 registerfile32_1 (
    .load(controllogic_1_registerload), .rsi1(r_splitter_1_rs1_i), .rsi2(r_splitter_1_rs2_i),
    .rdi(r_splitter_1_rd_i), .rd(outp), .Clock(clock_1_out), .rs1(registerfile32_1_rs1),
    .rs2(registerfile32_1_rs2));
  // ALU alu_1: pin names not known; wires that end beside it: controllogic_1_aluselect, registerfile32_1_rs1, registerfile32_1_rs2, outp
endmodule

module ControlLogic (
  input  [31:0] instruction,
  output [3:0] ALUselect,
  output registerLoad
);

  wire and_1_out, and_3_out;

  or or_1 (ALUselect[2], ALUselect[0], and_3_out);
  and and_1 (and_1_out, ~instruction[2], ~instruction[3], instruction[4], instruction[5], ~instruction[6], ~instruction[12], ~instruction[13], ~instruction[14], ~instruction[30]);  // AND_Gate
  and and_2 (ALUselect[3], ~instruction[2], ~instruction[3], instruction[4], instruction[5], ~instruction[6], ~instruction[12], ~instruction[13], ~instruction[14], instruction[30]);  // AND_Gate
  and and_3 (and_3_out, ~instruction[2], ~instruction[3], instruction[4], instruction[5], ~instruction[6], ~instruction[12], instruction[13], instruction[14], ~instruction[30]);  // AND_Gate
  and and_4 (ALUselect[0], ~instruction[2], ~instruction[3], instruction[4], instruction[5], ~instruction[6], instruction[12], instruction[13], instruction[14], ~instruction[30]);  // AND_Gate
  or or_2 (registerLoad, ALUselect[0], and_3_out, ALUselect[3], and_1_out);

  assign ALUselect[1] = ALUselect[2];

  // Notes on the sheet:
  //   Sub
  //   Or
  //   Add
  //   And
endmodule
